// Logisim project final_circuit.circ as structural Verilog: 10 circuits, main circuit main
module main (
);

  wire system_bus_1_buttons_e, system_bus_1_display_e, system_bus_1_ram_ctrl, system_bus_1_ram_m;
  wire [2:0] stalwart_cpu_1_ctrl;
  wire [3:0] system_bus_1_cpu_a_o, system_bus_1_ram_a;
  wire [6:0] display_handler_1_x1, display_handler_1_x10, display_handler_1_x100;
  wire [7:0] button_handler_1_o, ram_16x8_1_data_out, system_bus_1_cpu_d_o, system_bus_1_display;
  wire [9:0] button_7_out;

  Button button_1 (.out(button_7_out[1]));
  Button button_2 (.out(button_7_out[2]));
  Button button_3 (.out(button_7_out[5]));
  Button button_4 (.out(button_7_out[4]));
  Button button_5 (.out(button_7_out[8]));
  Button button_6 (.out(button_7_out[7]));
  Button button_7 (.out(button_7_out[0]));
  Button button_8 (.out(button_7_out[3]));
  Button button_9 (.out(button_7_out[6]));
  Button button_10 (.out(button_7_out[9]));
  Button_Handler button_handler_1 (.O(button_handler_1_o), .CS(system_bus_1_buttons_e), .I(button_7_out));
  RAM_16x8 ram_16x8_1 (
    .Mode(system_bus_1_ram_m), .Data_out(ram_16x8_1_data_out), .Data_in(ram_16x8_1_data_out),
    .CPU_CTRL(system_bus_1_ram_ctrl), .Address(system_bus_1_ram_a));  // open: CLK
  System_Bus system_bus_1 (
    .RAM_D_O(ram_16x8_1_data_out), .CPU_A_O(system_bus_1_cpu_a_o), .Buttons(button_handler_1_o),
    .CPU_D_I(system_bus_1_cpu_d_o), .CPU_A_I(system_bus_1_cpu_a_o), .Buttons_E(system_bus_1_buttons_e),
    .Display_E(system_bus_1_display_e), .RAM_M(system_bus_1_ram_m), .RAM_A(system_bus_1_ram_a),
    .RAM_D_I(ram_16x8_1_data_out), .CPU_CTRL(stalwart_cpu_1_ctrl), .CPU_D_O(system_bus_1_cpu_d_o),
    .Display(system_bus_1_display), .RAM_CTRL(system_bus_1_ram_ctrl));
  Stalwart_CPU stalwart_cpu_1 (
    .MBR_O(system_bus_1_cpu_d_o), .CTRL(stalwart_cpu_1_ctrl), .MAR_O(system_bus_1_cpu_a_o),
    .MBR_I(system_bus_1_cpu_d_o), .MAR_I(system_bus_1_cpu_a_o));
  _7_Segment_Display u_7_segment_display_1 (
    .g(display_handler_1_x100[0]), .f(display_handler_1_x100[1]), .a(display_handler_1_x100[2]),
    .b(display_handler_1_x100[3]), .e(display_handler_1_x100[6]), .d(display_handler_1_x100[5]),
    .c(display_handler_1_x100[4]));  // open: dp
  Display_Handler display_handler_1 (
    .x1(display_handler_1_x1), .x10(display_handler_1_x10), .x100(display_handler_1_x100),
    .IE(system_bus_1_display_e), .I(system_bus_1_display));
  _7_Segment_Display u_7_segment_display_2 (
    .g(display_handler_1_x10[0]), .f(display_handler_1_x10[1]), .a(display_handler_1_x10[2]),
    .b(display_handler_1_x10[3]), .e(display_handler_1_x10[6]), .d(display_handler_1_x10[5]),
    .c(display_handler_1_x10[4]));  // open: dp
  _7_Segment_Display u_7_segment_display_3 (
    .g(display_handler_1_x1[0]), .f(display_handler_1_x1[1]), .a(display_handler_1_x1[2]),
    .b(display_handler_1_x1[3]), .e(display_handler_1_x1[6]), .d(display_handler_1_x1[5]),
    .c(display_handler_1_x1[4]));  // open: dp
endmodule

module Button_Handler (
  input  [9:0] I,
  input  CS,
  output [7:0] O
);

  wire controlled_buffer_1_out, not_1_out, or_5_out;
  wire [3:0] byte_reg_1_o, or_4_out;
  wire [7:4] byte_reg_1_o_2;

  or or_1 (or_4_out[3], I[9], I[8]);
  or or_2 (or_4_out[2], I[7], I[6], I[5], I[4]);
  or or_3 (or_4_out[1], I[7], I[6], I[3], I[2]);
  or or_4 (or_4_out[0], I[9], I[7], I[5], I[3], I[1]);
  or or_5 (or_5_out, I[0], or_4_out[3], or_4_out[2], or_4_out[1], or_4_out[0]);
  assign controlled_buffer_1_out = not_1_out ? or_5_out : 1'bz;  // Controlled_Buffer controlled_buffer_1
  not not_1 (not_1_out, CS);
  Byte_Reg byte_reg_1 (
    .Chip_Select(1'b1), .I({byte_reg_1_o, or_4_out}), .Clock(controlled_buffer_1_out),
    .O({byte_reg_1_o_2, byte_reg_1_o}), .Mode_RW(controlled_buffer_1_out));
  assign O = CS ? {byte_reg_1_o_2, byte_reg_1_o} : 8'bz;  // Controlled_Buffer controlled_buffer_2
endmodule

module Display_Handler (
  input  [7:0] I,
  input  IE,
  output [6:0] x100,
  output [6:0] x10,
  output [6:0] x1
);


  // Notes on the sheet:
  //   Segment order: GFABCDE
endmodule

module System_Bus (
  input  [3:0] CPU_A_I,
  input  [7:0] CPU_D_I,
  input  [7:0] RAM_D_I,
  input  [7:0] Buttons,
  input  [2:0] CPU_CTRL,
  output [3:0] CPU_A_O,
  output [3:0] RAM_A,
  output [7:0] CPU_D_O,
  output [7:0] RAM_D_O,
  output [7:0] Display,
  output RAM_CTRL,
  output RAM_M,
  output Buttons_E,
  output Display_E
);


  // Notes on the sheet:
  //   Address bus: 4 bits
  //   Data bus: 8 bits
  //   Control Bus: Set size as required
endmodule

module RAM_16x8 (
  input  CLK,
  input  Mode,
  input  [3:0] Address,
  input  CPU_CTRL,
  input  [7:0] Data_in,
  output [7:0] Data_out
);

  wire controlled_buffer_1_out, controlled_buffer_2_out, d_ff_1_q, decoder_1_out0, decoder_1_out1,
       decoder_1_out2, decoder_1_out3, decoder_1_out4, decoder_1_out5, decoder_1_out6, decoder_1_out7,
       decoder_1_out8, decoder_1_out9, decoder_1_out10, decoder_1_out11, decoder_1_out12, decoder_1_out13,
       decoder_1_out14, decoder_1_out15, not_1_out, not_2_out, not_3_out, not_4_out, xor_1_out;
  wire [3:0] d_ff_5_q;
  wire [7:0] D_o, demultiplexer_1_out0, multiplexer_1_out, R_0_o;

  Byte_Reg R_0 (.Chip_Select(decoder_1_out0), .I(demultiplexer_1_out0), .Clock(CLK), .O(R_0_o), .Mode_RW(d_ff_1_q));
  Byte_Reg R_4 (.Chip_Select(decoder_1_out4), .I(demultiplexer_1_out0), .Clock(CLK), .O(R_0_o), .Mode_RW(d_ff_1_q));
  Byte_Reg R_8 (.Chip_Select(decoder_1_out8), .I(demultiplexer_1_out0), .Clock(CLK), .O(R_0_o), .Mode_RW(d_ff_1_q));
  Byte_Reg R_12 (.Chip_Select(decoder_1_out12), .I(demultiplexer_1_out0), .Clock(CLK), .O(R_0_o), .Mode_RW(d_ff_1_q));
  // Probe on R_0_o
  Multiplexer #(.width(8), .enable("false")) multiplexer_1 (
    .in0(R_0_o), .in1(Data_in), .out(multiplexer_1_out), .sel(d_ff_1_q));
  Byte_Reg R_1 (.Chip_Select(decoder_1_out1), .I(demultiplexer_1_out0), .Clock(CLK), .O(R_0_o), .Mode_RW(d_ff_1_q));
  Byte_Reg R_5 (.Chip_Select(decoder_1_out5), .I(demultiplexer_1_out0), .Clock(CLK), .O(R_0_o), .Mode_RW(d_ff_1_q));
  Byte_Reg R_9 (.Chip_Select(decoder_1_out9), .I(demultiplexer_1_out0), .Clock(CLK), .O(R_0_o), .Mode_RW(d_ff_1_q));
  Byte_Reg R_13 (.Chip_Select(decoder_1_out13), .I(demultiplexer_1_out0), .Clock(CLK), .O(R_0_o), .Mode_RW(d_ff_1_q));
  // Probe on multiplexer_1_out
  not not_1 (not_1_out, CLK);
  not not_2 (not_2_out, not_1_out);
  Byte_Reg D (.Chip_Select(1'b1), .I(multiplexer_1_out), .Clock(not_2_out), .O(D_o), .Mode_RW(not_4_out));
  // Probe on D_o
  Byte_Reg R_2 (.Chip_Select(decoder_1_out2), .I(demultiplexer_1_out0), .Clock(CLK), .O(R_0_o), .Mode_RW(d_ff_1_q));
  Byte_Reg R_6 (.Chip_Select(decoder_1_out6), .I(demultiplexer_1_out0), .Clock(CLK), .O(R_0_o), .Mode_RW(d_ff_1_q));
  Byte_Reg R_10 (.Chip_Select(decoder_1_out10), .I(demultiplexer_1_out0), .Clock(CLK), .O(R_0_o), .Mode_RW(d_ff_1_q));
  Byte_Reg R_14 (.Chip_Select(decoder_1_out14), .I(demultiplexer_1_out0), .Clock(CLK), .O(R_0_o), .Mode_RW(d_ff_1_q));
  not not_3 (not_3_out, d_ff_1_q);
  Demultiplexer #(.width(8), .enable("false")) demultiplexer_1 (
    .out0(demultiplexer_1_out0), .out1(Data_out), .in(D_o), .sel(not_3_out));
  Byte_Reg R_3 (.Chip_Select(decoder_1_out3), .I(demultiplexer_1_out0), .Clock(CLK), .O(R_0_o), .Mode_RW(d_ff_1_q));
  Byte_Reg R_7 (.Chip_Select(decoder_1_out7), .I(demultiplexer_1_out0), .Clock(CLK), .O(R_0_o), .Mode_RW(d_ff_1_q));
  Byte_Reg R_11 (.Chip_Select(decoder_1_out11), .I(demultiplexer_1_out0), .Clock(CLK), .O(R_0_o), .Mode_RW(d_ff_1_q));
  Byte_Reg R_15 (.Chip_Select(decoder_1_out15), .I(demultiplexer_1_out0), .Clock(CLK), .O(R_0_o), .Mode_RW(d_ff_1_q));
  Decoder #(.select(4)) decoder_1 (
    .out0(decoder_1_out0), .out1(decoder_1_out1), .out2(decoder_1_out2), .out3(decoder_1_out3),
    .out4(decoder_1_out4), .out5(decoder_1_out5), .out6(decoder_1_out6), .out7(decoder_1_out7),
    .out8(decoder_1_out8), .out9(decoder_1_out9), .out10(decoder_1_out10), .out11(decoder_1_out11),
    .out12(decoder_1_out12), .out13(decoder_1_out13), .out14(decoder_1_out14), .out15(decoder_1_out15),
    .sel(d_ff_5_q), .en(xor_1_out));
  xor xor_1 (xor_1_out, not_4_out, d_ff_1_q);
  D_Flip_Flop d_ff_1 (.D(Mode), .clk(controlled_buffer_1_out), .Q(d_ff_1_q));  // open: Qn, preset, reset
  assign controlled_buffer_1_out = not_4_out ? CLK : 1'bz;  // Controlled_Buffer controlled_buffer_1
  D_Flip_Flop d_ff_2 (.D(Address[3]), .clk(controlled_buffer_2_out), .Q(d_ff_5_q[3]));  // open: Qn, preset, reset
  assign controlled_buffer_2_out = not_4_out ? CLK : 1'bz;  // Controlled_Buffer controlled_buffer_2
  D_Flip_Flop d_ff_3 (.D(Address[2]), .clk(controlled_buffer_2_out), .Q(d_ff_5_q[2]));  // open: Qn, preset, reset
  not not_4 (not_4_out, CPU_CTRL);
  D_Flip_Flop d_ff_4 (.D(Address[1]), .clk(controlled_buffer_2_out), .Q(d_ff_5_q[1]));  // open: Qn, preset, reset
  D_Flip_Flop d_ff_5 (.D(Address[0]), .clk(controlled_buffer_2_out), .Q(d_ff_5_q[0]));  // open: Qn, preset, reset
endmodule

module Stalwart_CPU (
  input  [3:0] MAR_I,
  input  [7:0] MBR_I,
  output [3:0] MAR_O,
  output [7:0] MBR_O,
  output [2:0] CTRL
);

  // Byte_Reg MAR: pin names not known; wires that end beside it: MAR_I, MAR_O
  // Byte_Reg MBR: pin names not known; wires that end beside it: MBR_I, MBR_O
  Byte_Reg D0 ();  // open: Chip_Select, I, Clock, O, Mode_RW
  Byte_Reg D1 ();  // open: Chip_Select, I, Clock, O, Mode_RW
  ALU alu_1 ();  // open: A, Status, R, L, ALU_OP
  Nibble_Reg IC ();  // open: O, Chip_Select, Mode_RW, Clock, I
  Control_Unit control_unit_1 ();  // open: Gates, OP
  Byte_Reg IR ();  // open: Chip_Select, I, Clock, O, Mode_RW

  // Notes on the sheet:
  //   Fix byte length or spread over multiple pins
endmodule

module ALU (
  input  ALU_OP,
  input  [7:0] L,
  input  [7:0] R,
  output [2:0] Status,
  output [7:0] A
);

  wire [3:3] nibble_reg_1_o;

  Byte_Reg byte_reg_1 (.I(L));  // open: Chip_Select, Clock, O, Mode_RW
  Byte_Reg byte_reg_2 (.I(R));  // open: Chip_Select, Clock, O, Mode_RW
  Nibble_Reg nibble_reg_1 (.O({nibble_reg_1_o[3], Status}));  // open: Chip_Select, Mode_RW, Clock, I
  Byte_Reg byte_reg_3 (.O(A));  // open: Chip_Select, I, Clock, Mode_RW

  // Notes on the sheet:
  //   ALU operations: Add, Sub, Compare = Sub
  //   Neg, Zero, OF
endmodule

module Control_Unit (
  input  [7:0] OP,
  output [15:0] Gates
);


  // Notes on the sheet:
  //   Probably can reduce, depends on your instructions
  //   Random currently, either split or fix
endmodule

module Byte_Reg (
  input  [7:0] I,
  input  Clock,
  input  Mode_RW,
  input  Chip_Select,
  output [7:0] O
);

  wire and_1_out, and_2_out, not_1_out, not_2_out;
  wire [7:0] controlled_buffer_1_out, R_0_q;

  not not_1 (not_1_out, Clock);
  assign controlled_buffer_1_out = and_1_out ? I : 8'bz;  // Controlled_Buffer controlled_buffer_1
  not not_2 (not_2_out, not_1_out);
  and and_1 (and_1_out, Mode_RW, Chip_Select);
  and and_2 (and_2_out, Chip_Select, ~Mode_RW);  // AND_Gate
  D_Flip_Flop R_4 (.D(controlled_buffer_1_out[4]), .clk(not_2_out), .Q(R_0_q[4]));  // open: Qn, preset, reset
  D_Flip_Flop R_5 (.D(controlled_buffer_1_out[5]), .clk(not_2_out), .Q(R_0_q[5]));  // open: Qn, preset, reset
  D_Flip_Flop R_6 (.D(controlled_buffer_1_out[6]), .clk(not_2_out), .Q(R_0_q[6]));  // open: Qn, preset, reset
  D_Flip_Flop R_7 (.D(controlled_buffer_1_out[7]), .clk(not_2_out), .Q(R_0_q[7]));  // open: Qn, preset, reset
  assign O = and_2_out ? R_0_q : 8'bz;  // Controlled_Buffer controlled_buffer_2
  D_Flip_Flop R_0 (.D(controlled_buffer_1_out[0]), .clk(not_2_out), .Q(R_0_q[0]));  // open: Qn, preset, reset
  D_Flip_Flop R_1 (.D(controlled_buffer_1_out[1]), .clk(not_2_out), .Q(R_0_q[1]));  // open: Qn, preset, reset
  D_Flip_Flop R_2 (.D(controlled_buffer_1_out[2]), .clk(not_2_out), .Q(R_0_q[2]));  // open: Qn, preset, reset
  D_Flip_Flop R_3 (.D(controlled_buffer_1_out[3]), .clk(not_2_out), .Q(R_0_q[3]));  // open: Qn, preset, reset
endmodule

module Nibble_Reg (
  input  [3:0] I,
  input  Clock,
  input  Mode_RW,
  input  Chip_Select,
  output [3:0] O
);

  wire and_1_out, and_2_out, not_1_out, not_2_out;
  wire [3:0] controlled_buffer_1_out, d_ff_1_q;

  not not_1 (not_1_out, Clock);
  assign controlled_buffer_1_out = and_1_out ? I : 4'bz;  // Controlled_Buffer controlled_buffer_1
  not not_2 (not_2_out, not_1_out);
  and and_1 (and_1_out, Mode_RW, Chip_Select);
  and and_2 (and_2_out, Chip_Select, ~Mode_RW);  // AND_Gate
  D_Flip_Flop d_ff_1 (.D(controlled_buffer_1_out[0]), .clk(not_2_out), .Q(d_ff_1_q[0]));  // open: Qn, preset, reset
  D_Flip_Flop d_ff_2 (.D(controlled_buffer_1_out[1]), .clk(not_2_out), .Q(d_ff_1_q[1]));  // open: Qn, preset, reset
  D_Flip_Flop d_ff_3 (.D(controlled_buffer_1_out[2]), .clk(not_2_out), .Q(d_ff_1_q[2]));  // open: Qn, preset, reset
  D_Flip_Flop d_ff_4 (.D(controlled_buffer_1_out[3]), .clk(not_2_out), .Q(d_ff_1_q[3]));  // open: Qn, preset, reset
  assign O = and_2_out ? d_ff_1_q : 4'bz;  // Controlled_Buffer controlled_buffer_2
endmodule
